// Digital circuit CPU.dig as structural Verilog
module CPU (
  input  clk
);

  wire and_1_out, and_2_out, calc_imm_1_p2, CI, comparator_1_eq, Inv, op_0, wm, wreg, zero;
  wire [1:0] pcSource, RS;
  wire [2:0] funct3, ula_op;
  wire [4:0] rd, rs1, rs2;
  wire [6:0] funct7;
  wire [6:1] opcode;
  wire [31:0] add_2_s, BR_da, BR_db, imm, MD_d, multiplexer_1_out, multiplexer_2_out, multiplexer_4_out,
       not_1_out, pc_plus_4, PC_q, ula_1_s, ula_out;

  // Probe on pcSource
  Multiplexer #(.Selector_Bits(2), .Bits(32)) multiplexer_1 (
    .sel(pcSource), .in_0(pc_plus_4), .in_1(add_2_s), .in_2(ula_out), .in_3(ula_out), .out(multiplexer_1_out));
  and and_1 (and_1_out, op_0, 1'b1);
  // Probe on multiplexer_1_out
  Register #(.Bits(32)) PC (.D(multiplexer_1_out), .C(clk), .en(and_1_out), .Q(PC_q));
  // Probe on PC_q
  Add #(.Bits(32)) add_1 (.a(32'h4), .b(PC_q), .c_i(1'b0), .s(pc_plus_4));  // open: c_o
  ROM #(.AddrBits(24), .Bits(32)) IM (.A(PC_q[23:0]), .sel(1'b1), .D({funct7, rs2, rs1, funct3, rd, opcode, op_0}));
  Add #(.Bits(32)) add_2 (.a(PC_q), .b(imm), .c_i(1'b0), .s(add_2_s));  // open: c_o
  Comparator #(.Bits(5)) comparator_1 (.a({5{1'b0}}), .b(rd), .eq(comparator_1_eq));  // open: gt, lt
  and and_2 (and_2_out, ~comparator_1_eq, wreg);  // And
  // calc_imm calc_imm_1: pin names not known; wires that end beside it: {funct7, rs2, rs1, funct3, rd, opcode, op_0}, calc_imm_1_p2, imm
  // calc_type calc_type_1: pin names not known; wires that end beside it: {opcode, op_0}, calc_imm_1_p2
  CU cu_1 (
    .opc({opcode, op_0}), .f3(funct3), .f7(funct7), .zero(zero), .wreg(wreg), .ula_op(ula_op), .CI(CI),
    .resultSource(RS), .wm(wm), .PC_source(pcSource), .Inv(Inv));
  // Probe on imm
  RegisterFile #(.AddrBits(5), .Bits(32)) BR (
    .Din(multiplexer_4_out), .we(and_2_out), .Rw(rd), .C(clk), .Ra(rs1), .Rb(rs2), .Da(BR_da), .Db(BR_db));
  Multiplexer #(.Bits(32)) multiplexer_2 (.sel(CI), .in_0(BR_db), .in_1(imm), .out(multiplexer_2_out));
  ULA ula_1 (.op1(BR_da), .op2(multiplexer_2_out), .controle(ula_op), .s(ula_1_s), .Zero(zero));
  // Probe on ula_op
  assign not_1_out = ~ula_1_s;  // Not not_1, 32 bits wide
  Multiplexer #(.Bits(32)) multiplexer_3 (.sel(Inv), .in_0(ula_1_s), .in_1(not_1_out), .out(ula_out));
  // Probe on ula_out
  RAMDualPort #(.AddrBits(24), .Bits(32)) MD (.A(ula_out[23:0]), .Din(BR_db), .str(wm), .C(clk), .ld(1'b1), .D(MD_d));
  // Probe on RS
  Multiplexer #(.Selector_Bits(2), .Bits(32)) multiplexer_4 (
    .sel(RS), .in_0(ula_out), .in_1(MD_d), .in_2(pc_plus_4), .in_3(pc_plus_4), .out(multiplexer_4_out));

  // Other names for the same wires on the sheet: opcode[0] = op_0

  // Notes on the sheet:
  //   clk: Hz: 200
  //   HALT
  //   contents of IM (hex, n*v repeats v):
  //   513,0,0,0,1400593,0,0,0,100613,0,0,0,100693,0,0,0,8000ef,7*0,c52023
  //   ,0,0,0,d52223,0,0,0,200293,0,0,0,2b2da63,0,0,0,fff28313,0,0,0
  //   ,231313,0,0,0,a30333,0,0,0,32383,0,0,0,ffe28e13,0,0,0,2e1e13,0,0,0
  //   ,ae0e33,0,0,0,e2e83,0,0,0,1d38f33,0,0,0,1e32223,0,0,0,128293,0,0,0
  //   ,fd1ff06f,0,0,0,8067
endmodule
