// Digital circuit CU.dig as structural Verilog
module CU (
  input  [6:0] opc,
  input  [2:0] f3,
  input  [6:0] f7,
  input  zero,
  output wreg,
  output [2:0] ula_op,
  output CI,
  output [1:0] resultSource,
  output wm,
  output [1:0] PC_source,
  output Inv
);

  wire and_1_out, and_2_out, B, I, Ic, J, R;

  uni_interna uni_interna_1 (
    .op(opc), .f3(f3), .f7(f7), .R(R), .I(I), .S(wm), .J(J), .B(B), .Inv(Inv), .ula_op(ula_op), .Ic(Ic),
    .I_LW(resultSource[0]), .I_jalr(PC_source[1]));
  or or_1 (wreg, R, I, J);
  or or_2 (CI, I, wm);
  or or_3 (resultSource[1], J, PC_source[1]);
  and and_1 (and_1_out, J, ~PC_source[1]);  // And
  and and_2 (and_2_out, Inv, zero, ~PC_source[1]);  // And
  or or_4 (PC_source[0], and_1_out, and_2_out);

  // Other names for the same wires on the sheet: I_jalr = PC_source[1]; I_LW = resultSource[0]; S = wm
endmodule
