// Digital circuit Ic_ula.dig as structural Verilog
module Ic_ula (
  input  [2:0] f3,
  output [2:0] s
);

  wire and_1_out, and_2_out, and_3_out, and_4_out, and_5_out;

  and and_1 (and_1_out, ~f3[2], f3[1]);  // And
  and and_2 (and_2_out, f3[2], ~f3[0]);  // And
  and and_3 (and_3_out, f3[1], ~f3[0]);  // And
  and and_4 (and_4_out, f3[2], f3[1], ~f3[0]);  // And
  and and_5 (and_5_out, ~f3[1], f3[0]);  // And
  or or_1 (s[1], and_2_out, and_3_out);
  or or_2 (s[2], and_1_out, f3[0]);
  or or_3 (s[0], and_4_out, and_5_out);

  // Other names for the same wires on the sheet: C = f3[0]; B = f3[1]; A = f3[2]
endmodule
