// Digital circuit ULA.dig as structural Verilog
module ULA (
  input  [31:0] op1,
  input  [31:0] op2,
  input  [2:0] controle,
  output [31:0] s,
  output Zero
);

  wire comparator_1_eq, comparator_1_lt;
  wire [6:0] bitextender_1_out;
  wire [31:0] add_1_s, and_1_out, barrelshifter_1_out, bitextender_2_out, bitextender_3_out, or_1_out,
       sub_1_s, xor_1_out;

  BitExtender #(.inputBits(5), .outputBits(7)) bitextender_1 (.in(op2[4:0]), .out(bitextender_1_out));
  Add #(.Bits(32)) add_1 (.a(op1), .b(op2), .c_i(1'b0), .s(add_1_s));  // open: c_o
  Sub #(.Bits(32)) sub_1 (.a(op1), .b(op2), .c_i(1'b0), .s(sub_1_s));  // open: c_o
  assign xor_1_out = op1 ^ op2;  // XOr xor_1, 32 bits wide
  assign or_1_out = op1 | op2;  // Or or_1, 32 bits wide
  assign and_1_out = op1 & op2;  // And and_1, 32 bits wide
  Comparator #(.Signed("true"), .Bits(32)) comparator_1 (
    .a(op1), .b(op2), .eq(comparator_1_eq), .lt(comparator_1_lt));  // open: gt
  BarrelShifter #(.Bits(32), .barrelSigned("true")) barrelshifter_1 (
    .in(op1), .shift(bitextender_1_out), .out(barrelshifter_1_out));
  BitExtender #(.inputBits(1), .outputBits(32)) bitextender_2 (.in(comparator_1_eq), .out(bitextender_2_out));
  BitExtender #(.inputBits(1), .outputBits(32)) bitextender_3 (.in(comparator_1_lt), .out(bitextender_3_out));
  Multiplexer #(.Selector_Bits(3), .Bits(32)) multiplexer_1 (
    .sel(controle), .in_0(add_1_s), .in_1(sub_1_s), .in_2(xor_1_out), .in_3(or_1_out), .in_4(and_1_out),
    .in_5(barrelshifter_1_out), .in_6(bitextender_3_out), .in_7(bitextender_2_out), .out(s));
  Comparator #(.Bits(32)) comparator_2 (.a(s), .b({32{1'b0}}), .eq(Zero));  // open: gt, lt
endmodule
