// Digital circuit calc_imm.dig as structural Verilog
module calc_imm (
  input  [31:0] instr,
  input  [5:0] \type ,
  output [31:0] imm
);

  wire [31:0] B, I, J, S;

  BitExtender #(.inputBits(12), .outputBits(32)) bitextender_1 (.in(instr[31:20]), .out(I));
  BitExtender #(.inputBits(12), .outputBits(32)) bitextender_2 (
    .in({instr[7], instr[30:25], instr[11:8], 1'b0}), .out(B));
  BitExtender #(.inputBits(12), .outputBits(32)) bitextender_3 (.in({instr[20], instr[30:21], 1'b0}), .out(J));
  BitExtender #(.inputBits(12), .outputBits(32)) bitextender_4 (.in({instr[31:25], instr[11:7]}), .out(S));
  Multiplexer #(.Selector_Bits(2), .Bits(32)) multiplexer_1 (
    .sel(\type [1:0]), .in_0(I), .in_1(S), .in_2(B), .in_3(J), .out(imm));
  // Pins of 2 and 6 bits meet at \type 
  // Pins of 12 and 13 bits meet at {instr[31], instr[7], instr[30:25], instr[11:8], 1'b0}
  // Pins of 12 and 21 bits meet at {instr[31], instr[19:12], instr[20], instr[30:21], 1'b0}
endmodule
