// Digital circuit calc_type.dig as structural Verilog
module calc_type (
  input  [6:0] opcode,
  output [1:0] \type 
);

  wire and_1_out, and_2_out, not_1_out, not_2_out;

  and and_1 (and_1_out, opcode[6], not_1_out);
  not not_1 (not_1_out, opcode[2]);
  and and_2 (and_2_out, not_2_out, opcode[5]);
  not not_2 (not_2_out, opcode[6]);
  or or_1 (\type [1], opcode[3], and_1_out);
  or or_2 (\type [0], opcode[3], and_2_out);

  // Other names for the same wires on the sheet: E = opcode[2]; D = opcode[3]; C = opcode[4]; B = opcode[5];
  //   A = opcode[6]; S0 = \type [0]; S1 = \type [1]
endmodule
