// Digital circuit somador.dig as structural Verilog
module somador (
  input  [31:0] op1,
  input  [31:0] op2,
  output [31:0] s
);

  wire s1_c_o, s2_c_o, s3_c_o, s4_c_o, s5_c_o, s6_c_o, s7_c_o;

  Add #(.Bits(4)) s1 (.a(op1[3:0]), .b(op2[3:0]), .c_i(1'b0), .s(s[3:0]), .c_o(s1_c_o));
  Add #(.Bits(4)) s2 (.a(op1[7:4]), .b(op2[7:4]), .c_i(s1_c_o), .s(s[7:4]), .c_o(s2_c_o));
  Add #(.Bits(4)) s3 (.a(op1[11:8]), .b(op2[11:8]), .c_i(s2_c_o), .s(s[11:8]), .c_o(s3_c_o));
  Add #(.Bits(4)) s4 (.a(op1[15:12]), .b(op2[15:12]), .c_i(s3_c_o), .s(s[15:12]), .c_o(s4_c_o));
  Add #(.Bits(4)) s5 (.a(op1[19:16]), .b(op2[19:16]), .c_i(s4_c_o), .s(s[19:16]), .c_o(s5_c_o));
  Add #(.Bits(4)) s6 (.a(op1[23:20]), .b(op2[23:20]), .c_i(s5_c_o), .s(s[23:20]), .c_o(s6_c_o));
  Add #(.Bits(4)) s7 (.a(op1[27:24]), .b(op2[27:24]), .c_i(s6_c_o), .s(s[27:24]), .c_o(s7_c_o));
  Add #(.Bits(4)) s8 (.a(op1[31:28]), .b(op2[31:28]), .c_i(s7_c_o), .s(s[31:28]));  // open: c_o

  // Other names for the same wires on the sheet: s1_a[3:0] = op1[3:0]; s2_a[3:0] = op1[7:4]; s3_a[3:0] = op1[11:8];
  //   s4_a[3:0] = op1[15:12]; s5_a[3:0] = op1[19:16]; s6_a[3:0] = op1[23:20]; s7_a[3:0] = op1[27:24];
  //   s8_a[3:0] = op1[31:28]; s1_b[3:0] = op2[3:0]; s2_b[3:0] = op2[7:4]; s3_b[3:0] = op2[11:8];
  //   s4_b[3:0] = op2[15:12]; s5_b[3:0] = op2[19:16]; s6_b[3:0] = op2[23:20]; s7_b[3:0] = op2[27:24];
  //   s8_b[3:0] = op2[31:28]
endmodule
