// Digital circuit subtrator.dig as structural Verilog
module subtrator (
  input  [31:0] op1,
  input  [31:0] op2,
  output [31:0] s
);

  wire sub_1_c_o, sub_2_c_o, sub_3_c_o, sub_4_c_o, sub_5_c_o, sub_6_c_o, sub_7_c_o;

  Sub sub_1 (.a(op1[0]), .b(op2[0]), .c_i(1'b0), .s(s[0]), .c_o(sub_1_c_o));
  Sub sub_2 (.a(op1[4]), .b(op2[4]), .c_i(sub_1_c_o), .s(s[4]), .c_o(sub_2_c_o));
  Sub sub_3 (.a(op1[8]), .b(op2[8]), .c_i(sub_2_c_o), .s(s[8]), .c_o(sub_3_c_o));
  Sub sub_4 (.a(op1[12]), .b(op2[12]), .c_i(sub_3_c_o), .s(s[12]), .c_o(sub_4_c_o));
  Sub sub_5 (.a(op1[16]), .b(op2[16]), .c_i(sub_4_c_o), .s(s[16]), .c_o(sub_5_c_o));
  Sub sub_6 (.a(op1[20]), .b(op2[20]), .c_i(sub_5_c_o), .s(s[20]), .c_o(sub_6_c_o));
  Sub sub_7 (.a(op1[24]), .b(op2[24]), .c_i(sub_6_c_o), .s(s[24]), .c_o(sub_7_c_o));
  Sub sub_8 (.a(op1[28]), .b(op2[28]), .c_i(sub_7_c_o), .s(s[28]));  // open: c_o
  // Pins of 1 and 4 bits meet at op1[3:0]
  // Pins of 1 and 4 bits meet at op2[3:0]
  // Pins of 1 and 4 bits meet at s[3:0]
  // Pins of 1 and 4 bits meet at op1[7:4]
  // Pins of 1 and 4 bits meet at op2[7:4]
  // Pins of 1 and 4 bits meet at s[7:4]
  // Pins of 1 and 4 bits meet at op1[11:8]
  // Pins of 1 and 4 bits meet at op2[11:8]
  // Pins of 1 and 4 bits meet at s[11:8]
  // Pins of 1 and 4 bits meet at op1[15:12]
  // Pins of 1 and 4 bits meet at op2[15:12]
  // Pins of 1 and 4 bits meet at s[15:12]

  // Other names for the same wires on the sheet: s1_a[3:0] = op1[3:0]; s2_a[3:0] = op1[7:4]; s3_a[3:0] = op1[11:8];
  //   s4_a[3:0] = op1[15:12]; s5_a[3:0] = op1[19:16]; s6_a[3:0] = op1[23:20]; s7_a[3:0] = op1[27:24];
  //   s8_a[3:0] = op1[31:28]; s1_b[3:0] = op2[3:0]; s2_b[3:0] = op2[7:4]; s3_b[3:0] = op2[11:8];
  //   s4_b[3:0] = op2[15:12]; s5_b[3:0] = op2[19:16]; s6_b[3:0] = op2[23:20]; s7_b[3:0] = op2[27:24];
  //   s8_b[3:0] = op2[31:28]
endmodule
