// Digital circuit uni_interna.dig as structural Verilog
module uni_interna (
  input  [6:0] op,
  input  [2:0] f3,
  input  [6:0] f7,
  output R,
  output I,
  output S,
  output J,
  output B,
  output Inv,
  output [2:0] ula_op,
  output Ic,
  output I_LW,
  output I_jalr
);

  wire and_1_out, and_2_out, and_3_out, and_4_out, and_5_out, and_6_out, and_7_out, and_8_out, and_9_out,
       and_10_out, and_11_out, and_12_out, and_13_out, and_14_out, and_24_out, and_25_out, or_2_out, or_3_out;
  wire [1:0] and_22_out;
  wire [2:0] ic_ula_1_s, not_1_out, r_ula_1_s;

  and and_1 (and_1_out, op[1], ~op[2], ~op[3]);  // And
  and and_2 (and_2_out, op[4], op[5], ~op[6]);  // And
  and and_3 (and_3_out, op[1], ~op[2], ~op[3]);  // And
  and and_4 (and_4_out, op[4], ~op[5], ~op[6]);  // And
  and and_5 (and_5_out, op[1], ~op[2], ~op[3]);  // And
  and and_6 (and_6_out, ~op[4], ~op[5], ~op[6]);  // And
  and and_7 (and_7_out, op[1], op[2], ~op[3]);  // And
  and and_8 (and_8_out, ~op[4], op[5], op[6]);  // And
  and and_9 (and_9_out, op[1], ~op[2], ~op[3]);  // And
  and and_10 (and_10_out, ~op[4], op[5], op[6]);  // And
  and and_11 (and_11_out, op[1], ~op[2], ~op[3]);  // And
  and and_12 (and_12_out, ~op[4], op[5], ~op[6]);  // And
  and and_13 (and_13_out, op[1], op[2], op[3]);
  and and_14 (and_14_out, ~op[4], op[5], op[6]);  // And
  and and_15 (R, and_1_out, and_2_out);
  and and_16 (Ic, and_3_out, and_4_out);
  and and_17 (I_LW, and_5_out, and_6_out);
  and and_18 (I_jalr, and_7_out, and_8_out);
  and and_19 (B, and_9_out, and_10_out);
  and and_20 (S, and_11_out, and_12_out);
  and and_21 (J, and_13_out, and_14_out);
  R_ula r_ula_1 (.f3(f3), .f7_5(f7[5]), .S(r_ula_1_s));
  or or_1 (I, Ic, I_LW, I_jalr);
  Ic_ula ic_ula_1 (.f3(f3), .s(ic_ula_1_s));
  not not_1 (not_1_out[0], f3[2]);
  not not_2 (not_1_out[2], f3[1]);
  or or_2 (or_2_out, I_LW, I_jalr, S, I_LW, J);
  or or_3 (or_3_out, I_LW, I_jalr, S, I_LW, J);
  and and_22 (and_22_out[0], ~or_2_out, ~R);  // And
  and and_23 (and_22_out[1], ~or_3_out, ~Ic);  // And
  Multiplexer #(.Selector_Bits(2), .Bits(3)) multiplexer_1 (
    .sel(and_22_out), .in_0(3'b000), .in_1(ic_ula_1_s), .in_2(r_ula_1_s),
    .in_3({not_1_out[2], 1'b1, not_1_out[0]}), .out(ula_op));
  and and_24 (and_24_out, B, f3[0], ~f3[1], ~f3[2]);  // And
  and and_25 (and_25_out, B, f3[0], ~f3[1], f3[2]);  // And
  or or_4 (Inv, and_24_out, and_25_out);

  // Other names for the same wires on the sheet: f3_0 = f3[0]; f3_1 = f3[1]; f3_2 = f3[2]; f7_0 = f7[0]; f7_1 = f7[1];
  //   f7_2 = f7[2]; f7_3 = f7[3]; f7_4 = f7[4]; f7_5 = f7[5]; f7_6 = f7[6]
endmodule
